// Logisim project Untitled.circ as structural Verilog: 8 circuits, main circuit main
module main (
  output [7:0] out_1,
  output [7:0] out_2,
  output [7:0] out_3
);

  wire clock_1_out, not_1_out;

  ALU alu_1 (.Control(4'b0000), .B(8'h4), .A(8'h3), .out_4(out_3));
  not not_1 (not_1_out, 1'b1);
  ROM rom_1 (.addr({8{1'b1}}), .data(out_1));  // open: sel
  RAM #(.bus("separate")) ram_1 (
    .addr(8'h5), .din(8'h11), .data(out_2), .str(1'b1), .clk(clock_1_out), .ld(not_1_out));  // open: sel, clr
  Clock clock_1 (.out(clock_1_out));
endmodule

module RGandALU (
);

  wire clock_1_out, clock_2_out, clock_3_out, decoder_1_out0, decoder_1_out1, decoder_1_out2, decoder_1_out3,
       decoder_1_out4, decoder_1_out5, decoder_1_out6, decoder_1_out7, not_1_out;
  wire [2:0] bit_extender_4_out;
  wire [3:0] bit_extender_3_out;
  wire [7:0] adder_1_out, adder_2_out, adder_3_out, adder_4_out, adder_5_out, adder_6_out, adder_7_out,
       adder_8_out, alu_1_out_4, bit_extender_1_out, bit_extender_2_out, bit_extender_5_out,
       bit_extender_6_out, bit_extender_7_out, bit_extender_8_out, bit_extender_9_out, bit_extender_10_out,
       bit_extender_11_out, bit_extender_12_out, bit_extender_13_out, bit_extender_14_out,
       bit_extender_15_out, bit_extender_16_out, bit_extender_17_out, bit_extender_18_out,
       bit_extender_19_out, bit_extender_20_out, multiplexer_1_out, multiplexer_2_out, multiplexer_3_out,
       multiplexer_4_out, multiplexer_5_out, multiplexer_6_out, multiplexer_7_out, multiplexer_8_out,
       multiplexer_9_out, pcultra_1_cout, ram_1_data, registergroup_1_dout0, registergroup_1_dout1,
       registergroup_1_p0, registergroup_1_p1, subtractor_1_out, subtractor_2_out, subtractor_3_out,
       subtractor_4_out, subtractor_5_out, subtractor_6_out, subtractor_7_out, subtractor_8_out;
  wire [31:0] rom_1_data;

  PCUltra pcultra_1 (.Cout(pcultra_1_cout), .jumppos(bit_extender_1_out), .in_1(rom_1_data[28]));
  Clock clock_1 (.out(clock_1_out));
  Bit_Extender #(.in_width(32), .out_width(8)) bit_extender_1 (.in(rom_1_data), .out(bit_extender_1_out));
  ROM #(.dataWidth(32)) rom_1 (.addr(pcultra_1_cout), .data(rom_1_data));  // open: sel
  Bit_Extender #(.in_width(10), .out_width(8)) bit_extender_2 (.in(rom_1_data[15:6]), .out(bit_extender_2_out));
  Bit_Extender #(.in_width(6), .out_width(4)) bit_extender_3 (.in(rom_1_data[5:0]), .out(bit_extender_3_out));
  RegisterGroup registergroup_1 (
    .Din(multiplexer_1_out), .WriteAddr(rom_1_data[20:16]), .WriteEn(rom_1_data[31]), .CLK(clock_2_out),
    .Dout0(registergroup_1_dout0), .Addr1(rom_1_data[20:16]), .Dout1(registergroup_1_dout1),
    .Addr0(rom_1_data[25:21]), .P0(registergroup_1_p0), .P1(registergroup_1_p1));  // open: P2
  Clock clock_2 (.out(clock_2_out));
  Multiplexer #(.width(8)) multiplexer_1 (
    .in0(alu_1_out_4), .in1(ram_1_data), .out(multiplexer_1_out), .sel(rom_1_data[30]));  // open: en
  ALU alu_1 (.Control(bit_extender_3_out), .B(bit_extender_2_out), .A(registergroup_1_dout0), .out_4(alu_1_out_4));
  DotMatrix #(.matrixcols(8), .matrixrows(8)) dotmatrix_1 (
    .col0(registergroup_1_p1), .col1(registergroup_1_p0), .col2(registergroup_1_p0),
    .col3(registergroup_1_p1), .col4(registergroup_1_p1), .col5(registergroup_1_p0),
    .col6(registergroup_1_p1), .col7(registergroup_1_p0));
  not not_1 (not_1_out, rom_1_data[29]);
  RAM #(.bus("separate")) ram_1 (
    .addr(alu_1_out_4), .din(registergroup_1_dout1), .data(ram_1_data), .str(rom_1_data[29]),
    .clk(clock_3_out), .ld(not_1_out));  // open: sel, clr
  Clock clock_3 (.out(clock_3_out));
  Bit_Extender #(.out_width(3)) bit_extender_4 (.in(registergroup_1_p0), .out(bit_extender_4_out));
  DotMatrix #(.matrixcols(8), .matrixrows(8)) dotmatrix_2 (
    .col0(bit_extender_5_out), .col1(bit_extender_6_out), .col2(bit_extender_7_out),
    .col3(bit_extender_8_out), .col4(bit_extender_9_out), .col5(bit_extender_10_out),
    .col6(bit_extender_11_out), .col7(bit_extender_12_out));
  assign bit_extender_5_out = {{7{1'b0}}, registergroup_1_p1[0]};  // Bit_Extender bit_extender_5
  assign bit_extender_6_out = {{7{1'b0}}, registergroup_1_p1[1]};  // Bit_Extender bit_extender_6
  assign bit_extender_7_out = {{7{1'b0}}, registergroup_1_p1[2]};  // Bit_Extender bit_extender_7
  assign bit_extender_8_out = {{7{1'b0}}, registergroup_1_p1[3]};  // Bit_Extender bit_extender_8
  assign bit_extender_9_out = {{7{1'b0}}, registergroup_1_p1[4]};  // Bit_Extender bit_extender_9
  assign bit_extender_10_out = {{7{1'b0}}, registergroup_1_p1[5]};  // Bit_Extender bit_extender_10
  assign bit_extender_11_out = {{7{1'b0}}, registergroup_1_p1[6]};  // Bit_Extender bit_extender_11
  assign bit_extender_12_out = {{7{1'b0}}, registergroup_1_p1[7]};  // Bit_Extender bit_extender_12
  Decoder #(.select(3)) decoder_1 (
    .out0(decoder_1_out0), .out1(decoder_1_out1), .out2(decoder_1_out2), .out3(decoder_1_out3),
    .out4(decoder_1_out4), .out5(decoder_1_out5), .out6(decoder_1_out6), .out7(decoder_1_out7),
    .sel(bit_extender_4_out));  // open: en
  assign bit_extender_13_out = {{7{1'b0}}, decoder_1_out0};  // Bit_Extender bit_extender_13
  assign bit_extender_14_out = {{7{1'b0}}, decoder_1_out1};  // Bit_Extender bit_extender_14
  assign bit_extender_15_out = {{7{1'b0}}, decoder_1_out2};  // Bit_Extender bit_extender_15
  assign bit_extender_16_out = {{7{1'b0}}, decoder_1_out3};  // Bit_Extender bit_extender_16
  assign bit_extender_17_out = {{7{1'b0}}, decoder_1_out4};  // Bit_Extender bit_extender_17
  assign bit_extender_18_out = {{7{1'b0}}, decoder_1_out5};  // Bit_Extender bit_extender_18
  assign bit_extender_19_out = {{7{1'b0}}, decoder_1_out6};  // Bit_Extender bit_extender_19
  assign bit_extender_20_out = {{7{1'b0}}, decoder_1_out7};  // Bit_Extender bit_extender_20
  DotMatrix #(.matrixcols(8), .matrixrows(8)) dotmatrix_3 (
    .col0(multiplexer_2_out), .col1(multiplexer_3_out), .col2(multiplexer_4_out), .col3(multiplexer_5_out),
    .col4(multiplexer_6_out), .col5(multiplexer_7_out), .col6(multiplexer_8_out), .col7(multiplexer_9_out));
  Adder adder_1 (.a(registergroup_1_p1), .b(bit_extender_13_out), .out(adder_1_out));  // open: cin, cout
  Adder adder_2 (.a(registergroup_1_p1), .b(bit_extender_14_out), .out(adder_2_out));  // open: cin, cout
  Adder adder_3 (.a(registergroup_1_p1), .b(bit_extender_15_out), .out(adder_3_out));  // open: cin, cout
  Adder adder_4 (.a(registergroup_1_p1), .b(bit_extender_16_out), .out(adder_4_out));  // open: cin, cout
  Adder adder_5 (.a(registergroup_1_p1), .b(bit_extender_17_out), .out(adder_5_out));  // open: cin, cout
  Adder adder_6 (.a(registergroup_1_p1), .b(bit_extender_18_out), .out(adder_6_out));  // open: cin, cout
  Adder adder_7 (.a(registergroup_1_p1), .b(bit_extender_19_out), .out(adder_7_out));  // open: cin, cout
  Adder adder_8 (.a(registergroup_1_p1), .b(bit_extender_20_out), .out(adder_8_out));  // open: cin, cout
  Subtractor subtractor_1 (.a(adder_1_out), .b(8'h1), .out(subtractor_1_out));  // open: bin, bout
  Subtractor subtractor_2 (.a(adder_2_out), .b(8'h1), .out(subtractor_2_out));  // open: bin, bout
  Subtractor subtractor_3 (.a(adder_3_out), .b(8'h1), .out(subtractor_3_out));  // open: bin, bout
  Subtractor subtractor_4 (.a(adder_4_out), .b(8'h1), .out(subtractor_4_out));  // open: bin, bout
  Subtractor subtractor_5 (.a(adder_5_out), .b(8'h1), .out(subtractor_5_out));  // open: bin, bout
  Subtractor subtractor_6 (.a(adder_6_out), .b(8'h1), .out(subtractor_6_out));  // open: bin, bout
  Subtractor subtractor_7 (.a(adder_7_out), .b(8'h1), .out(subtractor_7_out));  // open: bin, bout
  Subtractor subtractor_8 (.a(adder_8_out), .b(8'h1), .out(subtractor_8_out));  // open: bin, bout
  Multiplexer #(.width(8)) multiplexer_2 (
    .in0(bit_extender_13_out), .in1(subtractor_1_out), .out(multiplexer_2_out), .sel(decoder_1_out0));  // open: en
  Multiplexer #(.width(8)) multiplexer_3 (
    .in0(bit_extender_14_out), .in1(subtractor_2_out), .out(multiplexer_3_out), .sel(decoder_1_out1));  // open: en
  Multiplexer #(.width(8)) multiplexer_4 (
    .in0(bit_extender_15_out), .in1(subtractor_3_out), .out(multiplexer_4_out), .sel(decoder_1_out2));  // open: en
  Multiplexer #(.width(8)) multiplexer_5 (
    .in0(bit_extender_16_out), .in1(subtractor_4_out), .out(multiplexer_5_out), .sel(decoder_1_out3));  // open: en
  Multiplexer #(.width(8)) multiplexer_6 (
    .in0(bit_extender_17_out), .in1(subtractor_5_out), .out(multiplexer_6_out), .sel(decoder_1_out4));  // open: en
  Multiplexer #(.width(8)) multiplexer_7 (
    .in0(bit_extender_18_out), .in1(subtractor_6_out), .out(multiplexer_7_out), .sel(decoder_1_out5));  // open: en
  Multiplexer #(.width(8)) multiplexer_8 (
    .in0(bit_extender_19_out), .in1(subtractor_7_out), .out(multiplexer_8_out), .sel(decoder_1_out6));  // open: en
  Multiplexer #(.width(8)) multiplexer_9 (
    .in0(bit_extender_20_out), .in1(subtractor_8_out), .out(multiplexer_9_out), .sel(decoder_1_out7));  // open: en

  // Notes on the sheet:
  //   contents of rom_1 (hex, n*v repeats v):
  //   84e00046 84e10106 24010006 24010046 84e60046 c4040006 c4050046 84e60106 84e60086 c4010006 84210064
  //   24010006 84e60046 c4040006 c4050046 84e60106 84e60086 10000009
endmodule

module AU (
  input  [7:0] num1,
  input  [7:0] num2,
  input  sel,
  output [7:0] sum
);

  wire not_2_out;
  wire [7:0] adder_1_out, multiplexer_1_out, not_1_out;

  assign not_1_out = ~num2;  // NOT_Gate not_1, 8 bits wide
  Adder adder_1 (.a(not_1_out), .b(8'h1), .out(adder_1_out));  // open: cin, cout
  not not_2 (not_2_out, sel);
  Multiplexer #(.width(8)) multiplexer_1 (
    .in0(num2), .in1(adder_1_out), .out(multiplexer_1_out), .sel(not_2_out));  // open: en
  Adder adder_2 (.a(num1), .b(multiplexer_1_out), .out(sum));  // open: cin, cout
endmodule

module LU (
  input  [7:0] a,
  input  [7:0] b,
  input  sel,
  output [7:0] ans
);

  wire not_1_out;
  wire [7:0] and_1_out, or_1_out;

  not not_1 (not_1_out, sel);
  assign and_1_out = a & b;  // AND_Gate and_1, 8 bits wide
  assign or_1_out = a | b;  // OR_Gate or_1, 8 bits wide
  Multiplexer #(.width(8)) multiplexer_1 (.in0(and_1_out), .in1(or_1_out), .out(ans), .sel(not_1_out));  // open: en
endmodule

module ALU (
  input  [3:0] Control,
  input  [7:0] B,
  input  [7:0] A,
  output [7:0] out_4
);

  wire not_1_out;
  wire [7:0] au_1_sum, lu_1_ans;

  LU lu_1 (.a(A), .b(B), .sel(Control[0]), .ans(lu_1_ans));
  AU au_1 (.num1(A), .num2(B), .sel(Control[1]), .sum(au_1_sum));
  not not_1 (not_1_out, Control[2]);
  Multiplexer #(.width(8)) multiplexer_1 (.in0(au_1_sum), .in1(lu_1_ans), .out(out_4), .sel(not_1_out));  // open: en
endmodule

module RegisterGroup (
  input  [4:0] Addr0,
  input  [4:0] Addr1,
  input  [7:0] Din,
  input  [4:0] WriteAddr,
  input  WriteEn,
  input  CLK,
  output [7:0] Dout0,
  output [7:0] Dout1,
  output [7:0] P0,
  output [7:0] P1,
  output [7:0] P2
);

  wire and_1_out, and_2_out, and_3_out, and_4_out, and_5_out, and_6_out, and_7_out, and_8_out,
       decoder_1_out0, decoder_1_out1, decoder_1_out2, decoder_1_out3, decoder_1_out4, decoder_1_out5,
       decoder_1_out6, decoder_1_out7;
  wire [7:0] register_1_q, register_2_q, register_3_q, register_4_q, register_8_q;

  Decoder #(.select(3)) decoder_1 (
    .out0(decoder_1_out0), .out1(decoder_1_out1), .out2(decoder_1_out2), .out3(decoder_1_out3),
    .out4(decoder_1_out4), .out5(decoder_1_out5), .out6(decoder_1_out6), .out7(decoder_1_out7),
    .sel(WriteAddr[2:0]));  // open: en
  and and_1 (and_1_out, decoder_1_out0, WriteEn);
  and and_2 (and_2_out, decoder_1_out1, WriteEn);
  and and_3 (and_3_out, decoder_1_out2, WriteEn);
  and and_4 (and_4_out, decoder_1_out3, WriteEn);
  and and_5 (and_5_out, decoder_1_out4, WriteEn);
  and and_6 (and_6_out, decoder_1_out5, WriteEn);
  and and_7 (and_7_out, decoder_1_out6, WriteEn);
  and and_8 (and_8_out, decoder_1_out7, WriteEn);
  Register register_1 (.D(Din), .en(and_1_out), .Q(register_1_q), .clk(CLK));  // open: clr
  Register register_2 (.D(Din), .en(and_2_out), .Q(register_2_q), .clk(CLK));  // open: clr
  Register register_3 (.D(Din), .en(and_3_out), .Q(register_3_q), .clk(CLK));  // open: clr
  Register register_4 (.D(Din), .en(and_4_out), .Q(register_4_q), .clk(CLK));  // open: clr
  Register register_5 (.D(Din), .en(and_5_out), .Q(P0), .clk(CLK));  // open: clr
  Register register_6 (.D(Din), .en(and_6_out), .Q(P1), .clk(CLK));  // open: clr
  Register register_7 (.D(Din), .en(and_7_out), .Q(P2), .clk(CLK));  // open: clr
  Register register_8 (.D(Din), .en(and_8_out), .Q(register_8_q), .clk(1'b1));  // open: clr
  Multiplexer #(.select(3), .width(8)) multiplexer_1 (
    .in0(register_1_q), .in1(register_2_q), .in2(register_3_q), .in3(register_4_q), .in4(P0), .in5(P1),
    .in6(P2), .in7(register_8_q), .out(Dout0), .sel(Addr0[2:0]));  // open: en
  Multiplexer #(.select(3), .width(8)) multiplexer_2 (
    .in0(register_1_q), .in1(register_2_q), .in2(register_3_q), .in3(register_4_q), .in4(P0), .in5(P1),
    .in6(P2), .in7(register_8_q), .out(Dout1), .sel(Addr1[2:0]));  // open: en
endmodule

module PC (
  input  in_1,
  output [7:0] Cout
);

  wire [7:0] adder_1_out;

  Register register_1 (.D(adder_1_out), .Q(Cout), .clk(in_1));  // open: en, clr
  Adder adder_1 (.a(Cout), .b(8'h1), .out(adder_1_out));  // open: cin, cout
endmodule

// PC
module PCUltra (
  input  in_1,
  input  [7:0] jumppos,
  output [7:0] Cout
);

  wire and_1_out, clock_1_out, not_1_out;
  wire [7:0] adder_1_out, multiplexer_1_out;

  Clock clock_1 (.out(clock_1_out));
  Multiplexer #(.width(8)) multiplexer_1 (
    .in0(jumppos), .in1(adder_1_out), .out(multiplexer_1_out), .sel(not_1_out));  // open: en
  Register clk (.D(multiplexer_1_out), .Q(Cout), .clk(clock_1_out));  // open: en, clr
  not not_1 (not_1_out, and_1_out);
  Adder adder_1 (.a(Cout), .b(8'h1), .out(adder_1_out));  // open: cin, cout
  and and_1 (and_1_out, 1'b1, in_1);
endmodule
